# Fritzing sketch fritzing sketch (saved by Fritzing 0.9.3b)
breadboards: 1

parts:
  Part1 = Arduino Mega 2560 (Rev3)
  R1 = Resistor [tolerance=±5% resistance=220 package=THT]
  LED1 = LED - 5mm [color="Green (565nm)" package="5 mm [THT]"]
  Part2 = SparkFun ESP8266 Thing
  R2 = Resistor [tolerance=±5% resistance=220 package=THT]
  0 = RFID USB Reader
  1 = RFID USB Reader  # not connected
  2 = RFID USB Reader  # not connected
  3 = RFID USB Reader

nets:
  VCC: Part1.3V3, Part2.VCC, Part2.GPIO15, 0.VCC
  GND: Part1.GND, LED1.cathode, Part2.GND, 0.TX-O
  N1: Part1.D0_RX0, R2.Pin_1
  N2: Part1.D1_TX0, Part2.U0TXO
  N3: Part1.D2_PWM, 0.GND
  N4: Part1.D3_PWM, 0.GNDT
  N5: Part1.D4_PWM, 3.GND
  N6: Part1.D5_PWM, 3.GNDT
  N7: Part1.D40, R1.Pin_1
  N8: Part1.D50, 0.ANT1
  N9: Part1.D51, 0.ANT2
  N10: Part1.D52, 0.CP
  N11: R1.Pin_0, LED1.anode
  N12: Part2.U0RXI, R2.Pin_0
